# Fritzing sketch CauldronBoc (saved by Fritzing 0.9.10b)
perfboards: 1

parts:
  R2 = Resistor [tolerance=±5% power=0.25 resistance=1k package=THT]
  R1 = Resistor [tolerance=±5% power=0.25 resistance=330 package=THT]
  C1 = Ceramic Capacitor [capacitance=100nF voltage=35V package="100 mil [THT, multilayer]"]
  C2 = Electrolytic Capacitor [capacitance=1µF voltage=35V package="100 mil [THT, electrolytic]"]
  M1 = Stepper Motor - Bipolar
  Part1 = Arduino Nano (Rev3.0)
  DRV_1 = DRV 8825 Stepper Motor Carrier, High Current [part_number="DRV 8825"]
  U1 = Voltage Regulator - Variable [package="TO220 [THT]"]
  Power_plug1 = Power plug
  C3 = Electrolytic Capacitor [capacitance=1µF voltage=35V package="100 mil [THT, electrolytic]"]

nets:
  GND: R2.Pin_0, C1.0, C2.-, Part1.GND, DRV_1.GROUND_ST/_MT, DRV_1.GROUND_LOG, Power_plug1.GND, C3.-
  N1: R2.Pin_1, R1.Pin_0, U1.ADJ
  N2: R1.Pin_1, C2.+, Part1.5V, U1.OUT
  N3: C1.1, DRV_1.VOLTAGE_ST/_MT, U1.IN, Power_plug1.VCC, C3.+
  N4: M1.A, DRV_1.OUT_2B
  N5: M1.C, DRV_1.OUT_2A
  N6: M1.B, DRV_1.OUT_1A
  N7: M1.D, DRV_1.OUT_1B
  N8: Part1.D2, DRV_1.DIRECTION
  N9: Part1.D3, DRV_1.STEP
  N10: Part1.D4, DRV_1.ENABLE
  N11: DRV_1.RESET, DRV_1.SLEEP
